# Fritzing sketch 接線圖 (saved by Fritzing 0.9.3b)
breadboards: 1

parts:
  R1 = Resistor [tolerance=±5% resistance=1M package=THT]
  R2 = Resistor [tolerance=±5% resistance=1M package=THT]
  R3 = Resistor [tolerance=±5% resistance=1M package=THT]
  R4 = Resistor [tolerance=±5% resistance=1M package=THT]
  R5 = Resistor [tolerance=±5% resistance=1M package=THT]
  R6 = Resistor [tolerance=±5% resistance=1M package=THT]
  元件1 = Arduino Uno (Rev3)
  C1 = Electrolytic Capacitor [capacitance=1µF package="100 mil [THT, electrolytic]"]
  C2 = Electrolytic Capacitor [capacitance=1µF package="100 mil [THT, electrolytic]"]
  C3 = Electrolytic Capacitor [capacitance=1µF package="100 mil [THT, electrolytic]"]
  C4 = Electrolytic Capacitor [capacitance=1µF package="100 mil [THT, electrolytic]"]
  C5 = Electrolytic Capacitor [capacitance=1µF package="100 mil [THT, electrolytic]"]  # not connected
  C6 = Electrolytic Capacitor [capacitance=1µF package="100 mil [THT, electrolytic]"]

nets:
  N1: R1.Pin_1, 元件1.D2
  N2: R2.Pin_0, 元件1.D9_PWM, C2.+
  N3: R2.Pin_1, 元件1.D3_PWM
  N4: R3.Pin_0, 元件1.D10_PWM/SS, C3.+
  N5: R3.Pin_1, 元件1.D4
  N6: R4.Pin_0, 元件1.D11_PWM/MOSI, C4.+
  N7: R4.Pin_1, 元件1.D5_PWM
  N8: R5.Pin_0, 元件1.D12/MISO
  N9: R5.Pin_1, 元件1.D6_PWM
  N10: R6.Pin_0, 元件1.D13/SCK, C6.+
  N11: R6.Pin_1, 元件1.D7
  N12: 元件1.D8, C1.+

notes:
  導電縫線(導體)
  找不到導電纖維的圖案 先用一顆電容代替
